# Fritzing sketch SPD Wiring Diagram(Miguel) (saved by Fritzing 0.9.3b)
breadboards: 1

parts:
  Part1 = Arduino Uno (Rev3) - ICSP
  RHT1 = Humidity and Temperature Sensor RHT03
  R1 = Resistor [tolerance=±5% resistance=10k package="2512 [SMD]"]
  R2 = Resistor [tolerance=±5% resistance=1k package=THT]
  R3 = Photocell (LDR) [package=THT]
  Chirp!_Soil_Moisture_Sensor1 = Chirp! Soil Moisture Sensor v2.7.3

nets:
  N1: Part1.A0, R2.Pin_0, R3.pin_0
  N2: Part1.A4/SDA, Chirp!_Soil_Moisture_Sensor1.pin_4
  N3: Part1.A5/SCL, Chirp!_Soil_Moisture_Sensor1.pin_2
  N4: Part1.D2, RHT1.Data-signal, R1.Pin_0
  5V: Part1.5V, RHT1.Vcc, R1.Pin_1, R3.pin_1, Chirp!_Soil_Moisture_Sensor1.Pin_1
  N5: Part1.GND, RHT1.GND_2, R2.Pin_1

notes:
  DHT22 Humidity Sensor
  -first pin: voltage source
  -second pin: data input
  -third pin: no connection
  -fourth pin: ground
  Soil Moisture Sensor
  -Vcc: Voltage source
  -SCL(green wire): I2C clock SCL pin
  -SDA(white wire): I2C data SDA pin
  -GND: ground
